# Fritzing sketch nrf24l01_xuWutpstYH (saved by Fritzing 0.9.3b)

parts:
  Composant1 = NRF24L01+ Breakout Board
  Composant2 = NRF24L01+ Breakout Board
  Receiver = Arduino Uno (Rev3)
  Transmitter = Arduino Uno (Rev3)
  R1 = Rotary Potentiometer (Small) [maximum_resistance=100kΩ package=THT]
  J1 = Basic Servo

nets:
  GND: Composant1.GND, Transmitter.GND, R1.leg2
  VCC: Composant1.VCC, Transmitter.3V3
  N1: Composant1.CE, Transmitter.D9_PWM
  N2: Composant1.CS, Transmitter.D10_PWM/SS
  N3: Composant1.SCK, Transmitter.D13/SCK
  N4: Composant1.MOSI, Transmitter.D11_PWM/MOSI
  N5: Composant1.MISO, Transmitter.D12/MISO
  N6: Composant1.IRQ, Transmitter.D8
  GND_2: Composant2.GND, Receiver.GND, J1.gnd
  VCC_2: Composant2.VCC, Receiver.3V3
  N7: Composant2.CE, Receiver.D9_PWM
  N8: Composant2.CS, Receiver.D10_PWM/SS
  N9: Composant2.SCK, Receiver.D13/SCK
  N10: Composant2.MOSI, Receiver.D11_PWM/MOSI
  N11: Composant2.MISO, Receiver.D12/MISO
  N12: Composant2.IRQ, Receiver.D8
  N13: Receiver.D3_PWM, J1.pulse
  5V: Receiver.5V, J1.vcc
  N14: Transmitter.A0, R1.wiper
  N15: Transmitter.5V, R1.leg1
